# Fritzing sketch raspberry pi off on (saved by Fritzing 0.9.3b)

parts:
  Raspberry_Pi_1 = Raspberry Pi 3 [part_number=RPI-3-V1.2]
  S3 = Pushbutton [package="[THT]"]

nets:
  N1: Raspberry_Pi_1.GPIO3, Raspberry_Pi_1.GIPO21, S3.Pin_3, S3.Pin_4
  N2: Raspberry_Pi_1.GND, S3.Pin_1, S3.Pin_2

notes:
  gnd
  halt
  boot
  press and release to boot
  press and hold for at least 6 seconds to shutdown
