# Fritzing sketch raspberry pi ups halt low battery (saved by Fritzing 0.9.3b)

parts:
  Raspberry_Pi_1 = Raspberry Pi 3 [part_number=RPI-3-V1.2]
  Part1 = PowerBoost 500 Charger
  U1 = LIPO-110mAh [package=lipo-110]
  S1 = Pushbutton [package="[THT]"]

nets:
  N1: Raspberry_Pi_1.GPIO3, S1.Pin_2
  N2: Raspberry_Pi_1.GND, S1.Pin_4
  N3: Part1.VBAT, U1.+, U1.-

notes:
  Connect PowerBoost input to power supply
  Connect PowerBoost output to Pi power
  halt
  lbo
  gnd
  boot

custom parts:
  PowerBoost 500 Charger: The PowerBoost 500C is a little DC/DC boost converter module that can be powered by any 3.7V LiIon/LiPoly battery, and convert the battery output to 5.2V DC for running your 5V projects. At its heart is a TPS61090 boost converter from TI. This boost converter chip has some really nice extras such as low battery detection, 2A internal switch, synchronous conversion, excellent efficiency, and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
